# Fritzing sketch breadboard (saved by Fritzing 1.0.5)
breadboards: 2

parts:
  IC1 = IC, DIP package, 20 pins [chip_label=PIC16F18346]  # not connected
  V1 = DC Power Supply [voltage=12V internal_resistance=1Ω max_current=0.1A]
  C1 = Electrolytic Capacitor [capacitance=10µF voltage=35V package="0807 [SMD, electrolytic]"]
  Part1 = OLED Monochrome 128x64 0.96 inch [part_number=326]  # not connected
  S1 = SWITCH-MOMENTARY-2 [package=tactile-pth-12mm]  # not connected
  S2 = SWITCH-MOMENTARY-2 [package=tactile-pth-12mm]  # not connected
  U1 = 74HC595 [package="DIP16 [THT]"]  # not connected
  U2 = 74HC595 [package="DIP16 [THT]"]
  R1 = Rotary Potentiometer (Small) [maximum_resistance=100kΩ knob_status=50% power=0.5W package=THT]  # not connected
  R2 = Rotary Potentiometer (Small) [maximum_resistance=100kΩ knob_status=50% power=0.5W package=THT]  # not connected
  J1 = Piezo Speaker  # not connected
  Q1 = TRANSISTOR_NPN [package=to-92]
  Q2 = TRANSISTOR_NPN [package=to-92]  # not connected
  Q3 = TRANSISTOR_NPN [package=to-92]  # not connected
  DI3 = 7 Segment Display
  DI4 = 7 Segment Display  # not connected

nets:
  N1: V1.Pin_2, C1.+, U2.VCC
  N2: V1.Pin_1, C1.-, U2.GND, Q1.E, DI3.Segment_DP
  N3: U2.Q1, DI3.Segment_A#10
  N4: U2.Q4, DI3.Segment_A#1
  N5: Q1.C, DI3.common_cathode

custom parts:
  OLED Monochrome 128x64 0.96 inch: These displays are small, only about 1" diameter, but very readable due to the high contrast of an OLED display. This display is made of 128x64 individual white OLED pixels, each one is turned on or off by the controller chip. Because the display makes its own light, no backlight is required. This reduces the power required to run the OLED and is why the display has such high contrast; we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
